// Logisim project Lab2_1.circ as structural Verilog: 6 circuits, main circuit main
module main (
);
endmodule

module circuitp1 (
);

  wire demultiplexer_1_out0, demultiplexer_1_out1, demultiplexer_2_out0, demultiplexer_2_out1,
       demultiplexer_3_out0, demultiplexer_3_out1, demultiplexer_4_out0, demultiplexer_4_out1, nand_1_out,
       nand_2_out, nand_3_out, nand_4_out, nand_5_out, nand_6_out, undriven, undriven_2, undriven_3,
       undriven_4, undriven_5;

  Demultiplexer #(.enable("false")) demultiplexer_1 (
    .out0(demultiplexer_1_out0), .out1(demultiplexer_1_out1), .in(undriven));  // open: sel
  Demultiplexer #(.enable("false")) demultiplexer_2 (
    .out0(demultiplexer_2_out0), .out1(demultiplexer_2_out1), .in(undriven_2));  // open: sel
  Demultiplexer #(.enable("false")) demultiplexer_3 (
    .out0(demultiplexer_3_out0), .out1(demultiplexer_3_out1), .in(undriven_3));  // open: sel
  nand nand_1 (nand_1_out, undriven_5, undriven_4);
  nand nand_2 (nand_2_out, demultiplexer_1_out0, demultiplexer_1_out1);
  nand nand_3 (nand_3_out, demultiplexer_2_out0, demultiplexer_2_out1);
  Demultiplexer #(.enable("false")) demultiplexer_4 (
    .out0(demultiplexer_4_out0), .out1(demultiplexer_4_out1), .in(nand_1_out));  // open: sel
  not nand_4 (nand_4_out, nand_2_out);  // NAND_Gate
  nand nand_5 (nand_5_out, demultiplexer_3_out0, demultiplexer_3_out1);
  nand nand_6 (nand_6_out, demultiplexer_4_out0, demultiplexer_4_out1);

  // Notes on the sheet:
  //   AND
  //   A
  //   B
  //   OR
  //   A
  //   B
  //   NOT
  //   A
  //   Output
  //   Output
  //   Output
endmodule

module circuitp2 (
);

  wire and_1_out, and_2_out, and_3_out, and_4_out, demultiplexer_1_out1, demultiplexer_2_out0,
       demultiplexer_2_out1, demultiplexer_3_out0, demultiplexer_3_out1, demultiplexer_4_out0,
       demultiplexer_4_out1, not_1_out, not_2_out, not_3_out, or_1_out, or_2_out, undriven, undriven_2,
       undriven_3, undriven_4, undriven_5;

  Demultiplexer #(.enable("false")) demultiplexer_1 (.out1(demultiplexer_1_out1), .in(undriven));  // open: out0, sel
  Demultiplexer #(.enable("false")) demultiplexer_2 (
    .out0(demultiplexer_2_out0), .out1(demultiplexer_2_out1), .in(undriven_2));  // open: sel
  Demultiplexer #(.enable("false")) demultiplexer_3 (
    .out0(demultiplexer_3_out0), .out1(demultiplexer_3_out1), .in(undriven_3));  // open: sel
  Demultiplexer #(.enable("false")) demultiplexer_4 (
    .out0(demultiplexer_4_out0), .out1(demultiplexer_4_out1), .in(undriven_4));  // open: sel
  and and_1 (and_1_out, undriven_5, demultiplexer_2_out0);
  not not_1 (not_1_out, demultiplexer_3_out0);
  not not_2 (not_2_out, demultiplexer_4_out0);
  not not_3 (not_3_out, and_1_out);
  or or_1 (or_1_out, demultiplexer_1_out1, demultiplexer_2_out1);
  and and_2 (and_2_out, not_1_out, demultiplexer_4_out1);
  and and_3 (and_3_out, demultiplexer_3_out1, not_2_out);
  and and_4 (and_4_out, not_3_out, or_1_out);
  or or_2 (or_2_out, and_2_out, and_3_out);

  // Notes on the sheet:
  //   A
  //   B
  //   A
  //   B
  //   Output
  //   Output
endmodule

module circuitp3 (
);

  wire and_1_out, and_2_out, demultiplexer_1_out0, demultiplexer_1_out1, demultiplexer_2_out0,
       demultiplexer_2_out1, demultiplexer_3_out0, demultiplexer_3_out1, demultiplexer_4_out0,
       demultiplexer_4_out1, or_1_out, undriven, undriven_2, undriven_3, xor_1_out, xor_2_out;

  Demultiplexer #(.enable("false")) demultiplexer_1 (
    .out0(demultiplexer_1_out0), .out1(demultiplexer_1_out1), .in(undriven));  // open: sel
  Demultiplexer #(.enable("false")) demultiplexer_2 (
    .out0(demultiplexer_2_out0), .out1(demultiplexer_2_out1), .in(undriven_2));  // open: sel
  xor xor_1 (xor_1_out, demultiplexer_1_out0, demultiplexer_2_out0);
  Demultiplexer #(.enable("false")) demultiplexer_3 (
    .out0(demultiplexer_3_out0), .out1(demultiplexer_3_out1), .in(undriven_3));  // open: sel
  and and_1 (and_1_out, demultiplexer_1_out1, demultiplexer_2_out1);
  Demultiplexer #(.enable("false")) demultiplexer_4 (
    .out0(demultiplexer_4_out0), .out1(demultiplexer_4_out1), .in(xor_1_out));  // open: sel
  xor xor_2 (xor_2_out, demultiplexer_4_out0, demultiplexer_3_out0);
  and and_2 (and_2_out, demultiplexer_3_out1, demultiplexer_4_out1);
  or or_1 (or_1_out, and_2_out, and_1_out);

  // Notes on the sheet:
  //   A
  //   B
  //   carry_in
  //   A
  //   FA
  //   B
  //   sum0
  //   carry_out0
  //   A
  //   FA
  //   B
  //   carry_in
  //   sum1
  //   carry_out1
  //   A
  //   FA
  //   B
  //   sum2
  //   carry_out2
  //   A
  //   B
  //   sum3
  //   FA
  //   carry_out
  //   Sum
  //   carry_out
endmodule

module circuitp4 (
);

  wire adder_1_p3, adder_1_p4, adder_1_p5, and_1_out, multiplexer_1_out, multiplexer_2_out,
       multiplexer_3_out, not_1_out, not_2_out, undriven, undriven_2;

  Multiplexer #(.enable("false")) multiplexer_1 (
    .in0(undriven), .in1(not_1_out), .out(multiplexer_1_out));  // open: sel
  not not_1 (not_1_out, undriven);
  not not_2 (not_2_out, undriven_2);
  Multiplexer #(.enable("false")) multiplexer_2 (
    .in0(undriven_2), .in1(not_2_out), .out(multiplexer_2_out));  // open: sel
  and and_1 (and_1_out, multiplexer_1_out, multiplexer_2_out);
  or or_1 (and_1_out, multiplexer_1_out, multiplexer_2_out);
  // Adder adder_1: pin names not known; wires that end beside it: multiplexer_1_out, multiplexer_2_out, adder_1_p3, adder_1_p4, adder_1_p5
  Multiplexer #(.enable("false")) multiplexer_3 (
    .in0(and_1_out), .in1(adder_1_p5), .out(multiplexer_3_out));  // open: sel

  // Notes on the sheet:
  //   A
  //   B
  //   carry_in
  //   carry_out
  //   result
endmodule

module circuitp5 (
);

  wire multiplexer_1_p4, xor_1_out;
  wire [7:0] adder_1_out, divider_1_out, undriven;

  Adder adder_1 (.a(undriven), .b(undriven), .out(adder_1_out));  // open: cin, cout
  Subtractor subtractor_1 (.a(undriven), .b(undriven), .out(adder_1_out));  // open: bin, bout
  Multiplier multiplier_1 (.a(undriven), .b(undriven), .out(adder_1_out));  // open: cin, cout
  Divider divider_1 (.a(undriven), .b(undriven), .out(divider_1_out));  // open: upper, rem
  xor xor_1 (xor_1_out, undriven[0], undriven[0]);
  Comparator comparator_1 (.a(undriven), .b(undriven), .eq(xor_1_out));  // open: gt, lt
  // Multiplexer #(.enable("false")) multiplexer_1: pin names not known; wires that end beside it: adder_1_out, divider_1_out, xor_1_out, multiplexer_1_p4
  // Pins of 1 and 8 bits meet at undriven

  // Notes on the sheet:
  //   A(0:7)
  //   B(0:7)
  //   Result
endmodule
